// Logisim project nad_or_not.circ as structural Verilog: 1 circuit, main circuit main
module main (
  input  in_1,
  input  in_2,
  input  in_3,
  input  in_4,
  input  in_5,
  input  in_6,
  output y1,
  output y0,
  output GS,
  output y1_2,
  output y0_2,
  output GS_2
);

  wire nand_1_out, nand_2_out, nand_3_out, nand_4_out, nand_5_out, nand_7_out, not_1_out;

  not not_1 (not_1_out, in_1);
  nand nand_1 (nand_1_out, in_4, in_4);
  nand nand_2 (nand_2_out, in_5, in_5);
  nand nand_3 (nand_3_out, in_6, in_6);
  and and_1 (y0, not_1_out, in_2);
  or or_1 (GS, in_3, in_2, in_1);
  nand nand_4 (nand_4_out, in_5, nand_1_out);
  nand nand_5 (nand_5_out, nand_3_out, nand_2_out);
  nand nand_6 (y0_2, nand_4_out, nand_4_out);
  nand nand_7 (nand_7_out, nand_5_out, nand_5_out);
  nand nand_8 (GS_2, nand_7_out, nand_1_out);

  assign y1 = in_1;
  assign y1_2 = in_4;

  // Notes on the sheet:
  //   x2
  //   x1
  //   x2
  //   x0
  //   x1
  //   x0
endmodule
