// Logisim project odejmowanie.circ as structural Verilog: 1 circuit, main circuit main
module main (
  input  a,
  input  b,
  input  c,
  output \pożyczka ,
  output \różnica 
);

  wire and_1_out, and_2_out, and_3_out, not_1_out;

  not not_1 (not_1_out, a);
  and and_1 (and_1_out, b, c);
  and and_2 (and_2_out, not_1_out, c);
  or or_1 (\pożyczka , and_1_out, and_2_out, and_3_out);
  and and_3 (and_3_out, not_1_out, b);
  xor xor_1 (\różnica , c, b, a);
endmodule
