// Logisim project transkoder.circ as structural Verilog: 1 circuit, main circuit main
module main (
  input  in_1,
  input  in_2,
  input  in_3,
  input  in_4
);

  wire [3:0] rom_1_data;

  Hex_Digit_Display hex_digit_display_1 (.value({in_4, in_3, in_2, in_1}));  // open: dp
  ROM #(.addrWidth(4), .dataWidth(4)) rom_1 (.addr({in_4, in_3, in_2, in_1}), .data(rom_1_data));
  Hex_Digit_Display hex_digit_display_2 (.value(rom_1_data));  // open: dp
  // Probe on rom_1_data[0]
  // Probe on rom_1_data[1]
  // Probe on rom_1_data[2]
  // Probe on rom_1_data[3]

  // Notes on the sheet:
  //   contents of rom_1 (hex, n*v repeats v):
  //   1 e b f 0 c 0 a 0 4 7 d 6 3 5 9
endmodule
